# Fritzing sketch Projet_Gaz_Detector (saved by Fritzing 0.9.3b)

parts:
  U1 = ESP8266 NodeMCU LoLin module
  J1 = Piezo Speaker
  Composant2 = MQ-7 breakout

nets:
  3V3: U1.3V3, J1.pin2, Composant2.VCC
  N1: U1.D5, J1.pin1
  GND: U1.GND, Composant2.GND

custom parts:
  ESP8266 NodeMCU LoLin module: ESP8266 based NodeMCU
  MQ-7 breakout: SKU: 101282
